# Fritzing sketch Bioprinter_Circuit_Lg (saved by Fritzing 0.9.2b)
breadboards: 1

parts:
  Part1 = Arduino Uno (Rev3)
  MD09B1 = A4988 Stepper Motor Driver Carrier
  M1 = Stepper Motor - Bipolar
  Q1 = MOSFET-NCHANNEL [package=to220v]  # not connected
  Syringe_Heater = Peltier Element
  Q3 = MOSFET-NCHANNEL [package=to220v]  # not connected
  Tubing_Heater = Peltier Element
  Nozzle_Heater = Peltier Element
  Q2 = MOSFET-NCHANNEL [package=to220v]  # not connected
  DS1 = DS18B20 1-Wire Temperature Sensor [part_number=DS18B20]
  DS2 = DS18B20 1-Wire Temperature Sensor [part_number=DS18B20]
  DS3 = DS18B20 1-Wire Temperature Sensor [part_number=DS18B20]
  Pullup = Resistor [tolerance=±5% resistance=4.7k package="1206 [SMD]"]
  J1 = Power Jack [package=power_jack_combo]
  Part2 = Arduino Uno (Rev3)
  Q4 = MOSFET-NCHANNEL [package=to220v]
  Q5 = MOSFET-NCHANNEL [package=to220v]
  Peltier = Peltier Element
  Fan = DC Motor
  C1 = Electrolytic Capacitor [capacitance=1µF package="100 mil [THT, electrolytic]"]
  R1 = Resistor [tolerance=±5% resistance=10k package=THT]
  Pulldown = Resistor [tolerance=±5% resistance=10k package=THT]
  R3 = Resistor [tolerance=±5% resistance=10k package=THT]
  R4 = Resistor [tolerance=±5% resistance=10k package=THT]
  R5 = Resistor [tolerance=±5% resistance=10k package=THT]
  J3 = female pin header, 2 pins [form="♀ (female)"]
  J4 = female pin header, 2 pins [form="♀ (female)"]  # not connected
  J5 = female pin header, 2 pins [form="♀ (female)"]
  J6 = female pin header, 2 pins [form="♀ (female)"]
  J7 = female pin header, 2 pins [form="♀ (female)"]

nets:
  N1: Part1.D8, MD09B1.STEP
  N2: Part1.D10_PWM/SS, J7.pin2
  N3: Part1.D11_PWM/MOSI, Part2.D11_PWM/MOSI, J7.pin1
  N4: Part1.D12/MISO, Part2.D12/MISO, J5.pin1
  N5: Part1.D13/SCK, Part2.D13/SCK, J3.pin2
  GND: Part1.GND, MD09B1.GROUND, DS1.GND, DS2.GND, DS3.GND, J1.GND, Part2.GND, Q4.S, Q5.S, C1.-, R1.Pin_0, Pulldown.Pin_0, R3.Pin_0, R4.Pin_0, R5.Pin_0, J3.pin1
  N6: Part1.D3_PWM, Pulldown.Pin_1
  N7: Part1.D4, MD09B1.DIR
  N8: Part1.D5_PWM, R3.Pin_1
  N9: Part1.D6_PWM, R1.Pin_1
  N10: Part1.D7, DS1.DQ, DS2.DQ, DS3.DQ, Pullup.Pin_1
  VDD: Part1.5V, MD09B1.VDD, DS1.VDD, DS2.VDD, DS3.VDD, Pullup.Pin_0
  VIN: Part1.VIN, Tubing_Heater.pin2, Nozzle_Heater.pin2, Part2.VIN, Fan.pin_2, C1.+
  N11: MD09B1.OUT_2B, M1.A
  N12: MD09B1.OUT_2A, M1.C
  N13: MD09B1.OUT_1A, M1.B
  N14: MD09B1.OUT_1B, M1.D
  N15: Syringe_Heater.pin2, J1.GNDBREAK, Peltier.pin2
  N16: Part2.D9_PWM, Q4.G, R4.Pin_1
  N17: Part2.D10_PWM/SS, J6.pin2
  N18: Part2.D6_PWM, Q5.G, R5.Pin_1
  N19: Q4.D, Peltier.pin1
  N20: Q5.D, Fan.pin_1

notes:
  RepRap SPI AUX-3 Header
  Interrupt signal
  from RAMPs
  To RepRap Board
  12V and GND
  12V Power Rail
  5V Power from Wall-Wart
